# Fritzing sketch MiniD1ESP32 (saved by Fritzing 0.9.3b)
breadboards: 1

parts:
  Componente1 = FTDI Basic Programmer
  LED1 = LED - 3mm [color="Red (633nm)" package="3 mm [THT]"]
  LED2 = LED - 3mm [color="Red (633nm)" package="3 mm [THT]"]
  LED3 = LED - 3mm [color="Green (565nm)" package="3 mm [THT]"]
  LED4 = LED - 3mm [color="Green (565nm)" package="3 mm [THT]"]
  S1 = Pushbutton [package="[THT]"]
  S2 = Pushbutton [package="[THT]"]
  R1 = Resistor [tolerance=±5% resistance=1k package="0402 [SMD]"]
  R2 = Resistor [tolerance=±5% resistance=1k package="0402 [SMD]"]
  R3 = Resistor [tolerance=±5% resistance=220 package="0402 [SMD]"]
  R4 = Resistor [tolerance=±5% resistance=220 package="0402 [SMD]"]
  R5 = Resistor [tolerance=±5% resistance=68 package="0402 [SMD]"]
  R6 = Resistor [tolerance=±5% resistance=68 package="0402 [SMD]"]
  A1 = MH-ET Live Minikit for ESP32

nets:
  N1: Componente1.RXI, A1.IO17
  N2: Componente1.TXO, A1.IO16
  N3: LED1.cathode, LED2.cathode, LED3.cathode, LED4.cathode, S2.Pin_1, S2.Pin_2, A1.GND
  N4: LED1.anode, R5.Pin_0
  N5: LED2.anode, R6.Pin_0
  N6: LED3.anode, R4.Pin_0
  N7: LED4.anode, R3.Pin_0
  N8: S1.Pin_1, S1.Pin_2, R1.Pin_1, R2.Pin_1, A1.3.3V
  N9: S1.Pin_3, S1.Pin_4, R2.Pin_0, A1.IO19
  N10: S2.Pin_3, S2.Pin_4, R1.Pin_0, A1.IO23
  N11: R3.Pin_1, A1.TCK
  N12: R4.Pin_1, A1.TMS
  N13: R5.Pin_1, A1.IO27
  N14: R6.Pin_1, A1.TDI

notes:
  Pulse

custom parts:
  MH-ET Live Minikit for ESP32: MH-ET Live Minikit for ESP32 ( http://mh.nodebb.com/topic/8/mh-et-live-minikit-for-esp32/2/) PCB footprint is invalid.
