# Fritzing sketch wemosD1R32 (saved by Fritzing 0.9.3b)
breadboards: 1

parts:
  WeMos_D1_R1 = WeMos D1 R2
  Componente1 = FTDI Basic Programmer
  LED1 = LED - 3mm [color="Red (633nm)" package="3 mm [THT]"]
  LED2 = LED - 3mm [color="Red (633nm)" package="3 mm [THT]"]
  LED3 = LED - 3mm [color="Green (565nm)" package="3 mm [THT]"]
  LED4 = LED - 3mm [color="Green (565nm)" package="3 mm [THT]"]
  S1 = Pushbutton [package="[THT]"]
  S2 = Pushbutton [package="[THT]"]
  R1 = Resistor [tolerance=±5% resistance=1k package="0402 [SMD]"]
  R2 = Resistor [tolerance=±5% resistance=1k package="0402 [SMD]"]
  R3 = Resistor [tolerance=±5% resistance=220 package="0402 [SMD]"]
  R4 = Resistor [tolerance=±5% resistance=220 package="0402 [SMD]"]
  R5 = Resistor [tolerance=±5% resistance=68 package="0402 [SMD]"]
  R6 = Resistor [tolerance=±5% resistance=68 package="0402 [SMD]"]

nets:
  N1: WeMos_D1_R1.D4, Componente1.RXI
  N2: WeMos_D1_R1.(D5), Componente1.TXO
  N3: WeMos_D1_R1.(D6), R5.Pin_1
  N4: WeMos_D1_R1.(D7), R4.Pin_1
  N5: WeMos_D1_R1.D8, R6.Pin_1
  N6: WeMos_D1_R1.D9, R3.Pin_1
  N7: WeMos_D1_R1.D11, S2.Pin_3, S2.Pin_4, R1.Pin_0
  N8: WeMos_D1_R1.D12, S1.Pin_3, S1.Pin_4, R2.Pin_0
  N9: WeMos_D1_R1.GND, LED1.cathode, LED2.cathode, LED3.cathode, LED4.cathode, S2.Pin_1, S2.Pin_2
  N10: WeMos_D1_R1.3.3V, S1.Pin_1, S1.Pin_2, R1.Pin_1, R2.Pin_1
  N11: LED1.anode, R5.Pin_0
  N12: LED2.anode, R6.Pin_0
  N13: LED3.anode, R4.Pin_0
  N14: LED4.anode, R3.Pin_0

notes:
  Pulse

custom parts:
  WeMos D1 R2: The D1 R2 is a mini wifi board based on the ESP-8266EX.
